# Fritzing sketch project fritzing diagram (saved by Fritzing 0.9.4)

parts:
  Mod1 = Raspberry Pi 4B
  DHT1 = DHT11 Humitidy and Temperature Sensor (3 pins)
  Part1 = LCD1602-I2C

nets:
  5V: Mod1.5V, DHT1.Plus, Part1.VCC
  N1: Mod1.GPIO2, Part1.SDA
  N2: Mod1.GPIO3, Part1.SCL
  GND: Mod1.GND, DHT1.Gnd, Part1.GND
  N3: Mod1.GPIO4, DHT1.Signal

custom parts:
  DHT11 Humitidy and Temperature Sensor (3 pins): DHT11 Humidity and Temperature Sensor (3 pins).
  LCD1602-I2C: A standard character display, usually with 2x16 characters. Comes in many colors with LCM1602 IIC attached.
